// Logisim project oisc.circ as structural Verilog: 1 circuit, main circuit main
module main (
  input  [7:0] DEBUG_IN
);

  wire buffer_3_out, CLK, demultiplexer_1_out2, demultiplexer_1_out3, demultiplexer_1_out7,
       demultiplexer_2_out0, demultiplexer_2_out1, demultiplexer_2_out2, demultiplexer_2_out3,
       demultiplexer_2_out4, demultiplexer_2_out5, demultiplexer_4_out0, demultiplexer_4_out1, MICRO_RST,
       not_1_out, not_2_out, OE_ADDR, OE_ALU, OE_DBGIN, OE_DBGOUT, OE_GENERAL, OE_IO, OE_MEM, OE_PC, OE_RAM,
       OE_ROM, SUFFIX_SELECT, WE_DBGOUT, WE_GENERAL, WE_HADDR, WE_IO, WE_LADDR, WE_MEM, WE_PC, WE_RAM, WE_X,
       WE_Y, Z_DETECT;
  wire [2:0] ADDRESS, OE_SELECT, SUFFIX_BITS, WE_SELECT;
  wire [3:0] MICRO_ADDR;
  wire [7:0] buffer_1_out, buffer_2_out, controlled_buffer_6_out, DATA, HADDR_q, HPC_q, LADDR_q, LPC_q,
       NOR_out, register_1_q, X_q, Y_q;
  wire [15:0] ADDR_DIRECT;

  Register #(.trigger("high")) X (.D(DATA), .en(1'b1), .Q(X_q), .clk(WE_X));  // open: clr
  Register #(.trigger("high")) Y (.D(DATA), .en(1'b1), .Q(Y_q), .clk(WE_Y));  // open: clr
  assign ADDR_DIRECT[15:8] = OE_PC ? HPC_q : 8'bz;  // Controlled_Buffer controlled_buffer_1
  Register #(.trigger("high")) HPC (.D(ADDR_DIRECT[15:8]), .Q(HPC_q), .clk(WE_PC));  // open: en, clr
  Register #(.trigger("high")) HADDR (.D(DATA), .Q(HADDR_q), .clk(WE_HADDR));  // open: en, clr
  assign ADDR_DIRECT[15:8] = OE_ADDR ? HADDR_q : 8'bz;  // Controlled_Buffer controlled_buffer_2
  assign NOR_out = ~(X_q | Y_q);  // NOR_Gate NOR, 8 bits wide
  assign DATA = OE_ALU ? NOR_out : 8'bz;  // Controlled_Buffer controlled_buffer_3
  assign ADDR_DIRECT[7:0] = OE_PC ? LPC_q : 8'bz;  // Controlled_Buffer controlled_buffer_4
  Register #(.trigger("high")) LPC (.D(ADDR_DIRECT[7:0]), .Q(LPC_q), .clk(WE_PC));  // open: en, clr
  Register #(.trigger("high")) LADDR (.D(DATA), .Q(LADDR_q), .clk(WE_LADDR));  // open: en, clr
  assign ADDR_DIRECT[7:0] = OE_ADDR ? LADDR_q : 8'bz;  // Controlled_Buffer controlled_buffer_5
  Multiplexer #(.width(3), .enable("false")) multiplexer_1 (
    .in0(ADDR_DIRECT[2:0]), .in1(SUFFIX_BITS), .out(ADDRESS), .sel(SUFFIX_SELECT));
  not not_1 (not_1_out, WE_RAM);
  assign buffer_1_out = DATA;  // Buffer buffer_1, 8 bits wide
  assign controlled_buffer_6_out = WE_RAM ? buffer_2_out : 8'bz;  // Controlled_Buffer controlled_buffer_6
  assign buffer_2_out = buffer_1_out;  // Buffer buffer_2, 8 bits wide
  RAM #(.addrWidth(14), .bus("asynch")) ram_1 (
    .addr({ADDR_DIRECT[13:3], ADDRESS}), .data(controlled_buffer_6_out), .ld(not_1_out));  // open: sel, clr
  assign DATA = OE_RAM ? controlled_buffer_6_out : 8'bz;  // Controlled_Buffer controlled_buffer_7
  nor Z (Z_DETECT, NOR_out[0], NOR_out[1], NOR_out[2], NOR_out[3], NOR_out[4], NOR_out[5], NOR_out[6], NOR_out[7]);
  // Probe on DATA
  // Probe on {ADDR_DIRECT[15:3], ADDRESS}
  Pull_Resistor pull_resistor_1 (.node({ADDR_DIRECT[15:3], ADDRESS}));
  Counter #(.width(4), .max('hf)) counter_1 (
    .Q(MICRO_ADDR), .clk(CLK), .clr(MICRO_RST));  // open: load, D, count, carry
  Clock CLK1 (.out(CLK));
  ROM #(.addrWidth(15)) rom_1 (.addr({ADDR_DIRECT[14:3], ADDRESS}), .data(DATA), .sel(OE_ROM));
  Demultiplexer #(.select(3)) demultiplexer_1 (
    .out0(WE_X), .out1(WE_Y), .out2(demultiplexer_1_out2), .out3(demultiplexer_1_out3), .out4(WE_HADDR),
    .out5(WE_LADDR), .out6(WE_PC), .out7(demultiplexer_1_out7), .in(WE_GENERAL), .sel(WE_SELECT), .en(1'b1));
  buf buffer_3 (buffer_3_out, OE_GENERAL);
  Demultiplexer #(.select(3)) demultiplexer_2 (
    .out0(demultiplexer_2_out0), .out1(demultiplexer_2_out1), .out2(demultiplexer_2_out2),
    .out3(demultiplexer_2_out3), .out4(demultiplexer_2_out4), .out5(demultiplexer_2_out5), .out6(OE_PC),
    .out7(OE_ADDR), .in(buffer_3_out), .sel(OE_SELECT), .en(1'b1));
  not not_2 (not_2_out, CLK);
  Demultiplexer #(.select(2), .enable("false")) demultiplexer_3 (
    .out2(WE_RAM), .out3(WE_IO), .in(WE_MEM), .sel(ADDR_DIRECT[15:14]));  // open: out0, out1
  Demultiplexer #(.select(2), .enable("false")) demultiplexer_4 (
    .out0(demultiplexer_4_out0), .out1(demultiplexer_4_out1), .out2(OE_RAM), .out3(OE_IO), .in(OE_MEM),
    .sel(ADDR_DIRECT[15:14]));
  ROM #(.addrWidth(5), .dataWidth(16)) rom_2 (
    .addr({Z_DETECT, MICRO_ADDR}),
    .data({OE_GENERAL, OE_SELECT, WE_GENERAL, WE_SELECT, SUFFIX_SELECT, SUFFIX_BITS, OE_ALU, WE_MEM, OE_MEM, MICRO_RST}),
    .sel(not_2_out));
  Pull_Resistor pull_resistor_2 (.node({OE_GENERAL, OE_SELECT, WE_GENERAL, WE_SELECT, SUFFIX_SELECT, SUFFIX_BITS, OE_ALU, WE_MEM, OE_MEM, MICRO_RST}));
  or or_1 (OE_ROM, demultiplexer_4_out0, demultiplexer_4_out1);
  LED led_1 (.in(DEBUG_IN[7]));
  LED led_2 (.in(DEBUG_IN[6]));
  LED led_3 (.in(DEBUG_IN[4]));
  LED led_4 (.in(DEBUG_IN[5]));
  Register #(.trigger("high")) register_1 (.D(DATA), .Q(register_1_q), .clk(WE_DBGOUT));  // open: en, clr
  LED led_5 (.in(register_1_q[5]));
  LED led_6 (.in(register_1_q[4]));
  LED led_7 (.in(register_1_q[6]));
  LED led_8 (.in(register_1_q[7]));
  Demultiplexer #(.enable("false")) demultiplexer_5 (.out0(OE_DBGOUT), .out1(OE_DBGIN), .in(OE_IO), .sel(ADDRESS[0]));
  Demultiplexer #(.enable("false")) demultiplexer_6 (.out0(WE_DBGOUT), .in(WE_IO), .sel(ADDRESS[0]));  // open: out1
  assign DATA = OE_DBGIN ? DEBUG_IN : 8'bz;  // Controlled_Buffer controlled_buffer_8
  LED led_9 (.in(DEBUG_IN[3]));
  LED led_10 (.in(DEBUG_IN[2]));
  LED led_11 (.in(DEBUG_IN[0]));
  LED led_12 (.in(DEBUG_IN[1]));
  assign DATA = OE_DBGOUT ? {8{1'b0}} : 8'bz;  // Controlled_Buffer controlled_buffer_9
  LED led_13 (.in(register_1_q[1]));
  LED led_14 (.in(register_1_q[0]));
  LED led_15 (.in(register_1_q[2]));
  LED led_16 (.in(register_1_q[3]));

  // Other names for the same wires on the sheet: ADDRESS[15:3] = ADDR_DIRECT[15:3]

  // Notes on the sheet:
  //   RAM
  //   ALU
  //   REGISTERS
  //   buffered for data holdoff (caps irl)
  //   PROGRAM ROM
  //   MAPPED MEMORY
  //   contents of rom_1 (hex, n*v repeats v):
  //   bf ff 0 70 0 8 0 8 bf ff c0 1 0 10 0 10 bf ff 0 71 0 18 0 18 bf fe 0 70 0 20 0 20 bf fe bf ff 0 28 0
  //   28 bf fe bf fe 0 30 0 50 bf ff 0 70 0 38 0 38 bf ff 0 72 0 40 0 40 c0 0 bf ff 0 48 0 48 bf ff bf ff
  //   4*0 bf ff 0 70 0 58 0 58 bf ff 0 73 0 60 0 60 c0 0 bf ff 0 68 0 68 bf ff bf ff 4*0 ff f 0 1
  //   MICROCODE
  //   contents of rom_2 (hex, n*v repeats v):
  //   eca2 edb2 f902 ec82 ed92 f802 f00c ecc2 edd2 fe00 1 5*0 eca2 edb2 f902 ec82 ed92 f802 f00c ece2 edf2
  //   fe00 1
  //   I/O
endmodule
